// Logisim project von-neumann - Kopie.circ as structural Verilog: 8 circuits, main circuit 8bit adder
module _8bit_adder (
  input  in_1,
  input  in_2,
  input  in_3,
  input  in_4,
  input  in_5,
  input  in_6,
  input  in_7,
  input  in_8,
  input  subtract,
  output out_10,
  output out_11,
  output out_12,
  output out_13,
  output out_14
);

  wire and_1_out, and_2_out, and_3_out, and_4_out, and_5_out, and_6_out, and_7_out, and_8_out, or_1_out,
       or_2_out, or_3_out, xor_1_out, xor_2_out, xor_3_out, xor_4_out, xor_5_out, xor_6_out, xor_7_out,
       xor_8_out;

  xor xor_1 (xor_1_out, in_5, subtract);
  xor xor_2 (xor_2_out, in_6, subtract);
  xor xor_3 (xor_3_out, in_7, subtract);
  xor xor_4 (xor_4_out, in_8, subtract);
  and and_1 (and_1_out, or_1_out, xor_1_out);
  xor xor_5 (xor_5_out, or_1_out, xor_1_out);
  and and_2 (and_2_out, or_2_out, xor_2_out);
  xor xor_6 (xor_6_out, or_2_out, xor_2_out);
  and and_3 (and_3_out, or_3_out, xor_3_out);
  xor xor_7 (xor_7_out, or_3_out, xor_3_out);
  and and_4 (and_4_out, subtract, xor_4_out);
  xor xor_8 (xor_8_out, subtract, xor_4_out);
  and and_5 (and_5_out, xor_5_out, in_1);
  xor xor_9 (out_11, xor_5_out, in_1);
  and and_6 (and_6_out, xor_6_out, in_2);
  xor xor_10 (out_12, xor_6_out, in_2);
  and and_7 (and_7_out, xor_7_out, in_3);
  xor xor_11 (out_13, xor_7_out, in_3);
  and and_8 (and_8_out, xor_8_out, in_4);
  xor xor_12 (out_14, xor_8_out, in_4);
  or or_1 (or_1_out, and_6_out, and_2_out);
  or or_2 (or_2_out, and_7_out, and_3_out);
  or or_3 (or_3_out, and_8_out, and_4_out);
  or or_4 (out_10, and_5_out, and_1_out);
endmodule

module von_neumann (
  input  writing_mode,
  input  [13:0] in_2,
  input  [7:0] in_3,
  input  clear,
  input  programming_mode,
  input  update,
  input  [7:0] in_7,
  input  in_8,
  input  in_9,
  output [13:0] out_10,
  output [7:0] out_11,
  output [7:0] out_12,
  output [7:0] out_13,
  output [7:0] out_14
);

  wire add, \and , and_1_out, and_2_out, and_3_out, and_4_out, and_5_out, button_1_out, clk, clock_1_out,
       cmp, comparator_1_eq, comparator_2_eq, controlled_buffer_1_out, controlled_buffer_7_out,
       controlled_buffer_18_out, controlled_buffer_25_out, \end , jeq, jgt, jlt, jmp, ld,
       n8bit_adder_1_out_18, \not , not_1_out, not_2_out, not_3_out, not_4_out, not_5_out, not_6_out,
       not_8_out, not_9_out, not_10_out, not_11_out, not_12_out, \or , or_1_out, or_2_out, or_3_out,
       or_4_out, or_6_out, out, psh, st, sub, v_a;
  wire [4:0] register_1_q;
  wire [7:0] addr, and_6_out, controlled_buffer_2_out, controlled_buffer_3_out, controlled_buffer_4_out,
       controlled_buffer_5_out, controlled_buffer_6_out, controlled_buffer_8_out, controlled_buffer_9_out,
       controlled_buffer_10_out, controlled_buffer_11_out, controlled_buffer_12_out,
       controlled_buffer_15_out, controlled_buffer_20_out, n8bit_adder_1_out_26, not_7_out, op_counter,
       or_5_out, ram_1_data;
  wire [7:5] n8bit_comperator_1_out_17;
  wire [13:0] controlled_buffer_27_out;

  Button button_1 (.out(button_1_out));
  not not_1 (not_1_out, button_1_out);
  and and_1 (and_1_out, jlt, out_11[2]);
  and and_2 (and_2_out, jgt, out_11[0]);
  and and_3 (and_3_out, jeq, out_11[1]);
  Clock #(.highDuration(10), .lowDuration(10)) clock_1 (.out(clock_1_out));
  Comparator #(.mode("unsigned")) comparator_1 (.a(op_counter), .b({8{1'b0}}), .eq(comparator_1_eq));  // open: gt, lt
  and and_4 (and_4_out, comparator_1_eq, not_1_out);
  or or_1 (or_1_out, and_1_out, and_2_out, and_3_out, jmp, \end );
  Multiplexer multiplexer_1 (.in0(clock_1_out), .in1(1'b0), .out(clk), .sel(and_4_out));  // open: en
  assign controlled_buffer_1_out = not_5_out ? clk : 1'bz;  // Controlled_Buffer controlled_buffer_1
  address_counter operation_counter (
    .clock(controlled_buffer_1_out), .val(in_7), .subtract(in_8), .out_6(op_counter), .jump_to(addr),
    .jump_mode(or_1_out));
  assign controlled_buffer_2_out = or_3_out ? out_13 : 8'bz;  // Controlled_Buffer controlled_buffer_2
  assign controlled_buffer_3_out = cmp ? out_13 : 8'bz;  // Controlled_Buffer controlled_buffer_3
  assign controlled_buffer_4_out = \and  ? out_13 : 8'bz;  // Controlled_Buffer controlled_buffer_4
  assign controlled_buffer_5_out = \or  ? out_13 : 8'bz;  // Controlled_Buffer controlled_buffer_5
  assign controlled_buffer_6_out = programming_mode ? in_3 : 8'bz;  // Controlled_Buffer controlled_buffer_6
  not not_2 (not_2_out, programming_mode);
  or or_2 (or_2_out, ld, or_4_out);
  assign controlled_buffer_7_out = st ? clk : 1'bz;  // Controlled_Buffer controlled_buffer_7
  or or_3 (or_3_out, add, sub);
  assign controlled_buffer_8_out = or_3_out ? out_11 : 8'bz;  // Controlled_Buffer controlled_buffer_8
  assign controlled_buffer_9_out = cmp ? out_11 : 8'bz;  // Controlled_Buffer controlled_buffer_9
  assign controlled_buffer_10_out = \and  ? out_11 : 8'bz;  // Controlled_Buffer controlled_buffer_10
  assign controlled_buffer_11_out = \or  ? out_11 : 8'bz;  // Controlled_Buffer controlled_buffer_11
  assign controlled_buffer_12_out = \not  ? out_13 : 8'bz;  // Controlled_Buffer controlled_buffer_12
  assign controlled_buffer_6_out = not_2_out ? op_counter : 8'bz;  // Controlled_Buffer controlled_buffer_13
  not not_3 (not_3_out, comparator_2_eq);
  Comparator #(.mode("unsigned")) comparator_2 (.a(out_11), .b(out_14), .eq(comparator_2_eq));  // open: gt, lt
  RAM ram_1 (.addr(addr), .data(ram_1_data), .clk(controlled_buffer_7_out), .ld(or_2_out));  // open: sel, clr
  or or_4 (or_4_out, add, sub, cmp, \and , \or , \not );
  assign out_10 = writing_mode ? in_2 : 14'bz;  // Controlled_Buffer controlled_buffer_14
  not not_4 (not_4_out, writing_mode);
  not not_5 (not_5_out, and_5_out);
  and and_5 (and_5_out, psh, not_3_out);
  assign controlled_buffer_15_out = v_a ? addr : 8'bz;  // Controlled_Buffer controlled_buffer_15
  not not_6 (not_6_out, v_a);
  assign controlled_buffer_15_out = not_6_out ? ram_1_data : 8'bz;  // Controlled_Buffer controlled_buffer_16
  assign ram_1_data = st ? out_11 : 8'bz;  // Controlled_Buffer controlled_buffer_17
  _8bit_adder_2 u_8bit_adder_1 (
    .out_18(n8bit_adder_1_out_18), .out_19(n8bit_adder_1_out_26[7]), .out_20(n8bit_adder_1_out_26[6]),
    .in_1(controlled_buffer_8_out[7]), .out_21(n8bit_adder_1_out_26[5]), .in_2(controlled_buffer_8_out[6]),
    .in_3(controlled_buffer_8_out[5]), .in_4(controlled_buffer_8_out[4]), .out_22(n8bit_adder_1_out_26[4]),
    .in_5(controlled_buffer_8_out[3]), .in_6(controlled_buffer_8_out[2]), .in_7(controlled_buffer_8_out[1]),
    .in_8(controlled_buffer_8_out[0]), .in_9(controlled_buffer_2_out[7]), .in_10(controlled_buffer_2_out[6]),
    .in_11(controlled_buffer_2_out[5]), .in_12(controlled_buffer_2_out[4]),
    .in_13(controlled_buffer_2_out[3]), .in_14(controlled_buffer_2_out[2]),
    .in_15(controlled_buffer_2_out[1]), .in_16(controlled_buffer_2_out[0]), .subtract(sub),
    .out_23(n8bit_adder_1_out_26[3]), .out_24(n8bit_adder_1_out_26[2]), .out_25(n8bit_adder_1_out_26[1]),
    .out_26(n8bit_adder_1_out_26[0]));
  _8bit_comperator u_8bit_comperator_1 (
    .in_1(controlled_buffer_9_out[7]), .in_2(controlled_buffer_9_out[6]), .in_3(controlled_buffer_9_out[5]),
    .in_4(controlled_buffer_9_out[4]), .in_5(controlled_buffer_9_out[3]), .in_6(controlled_buffer_9_out[2]),
    .in_7(controlled_buffer_9_out[1]), .in_8(controlled_buffer_9_out[0]), .in_9(controlled_buffer_3_out[7]),
    .in_10(controlled_buffer_3_out[6]), .in_11(controlled_buffer_3_out[5]),
    .in_12(controlled_buffer_3_out[4]), .in_13(controlled_buffer_3_out[3]),
    .in_14(controlled_buffer_3_out[2]), .in_15(controlled_buffer_3_out[1]),
    .in_16(controlled_buffer_3_out[0]), .out_17(n8bit_comperator_1_out_17[5]),
    .out_18(n8bit_comperator_1_out_17[6]), .out_19(n8bit_comperator_1_out_17[7]));
  and and_6 (and_6_out[0], controlled_buffer_10_out[0], controlled_buffer_4_out[0]);
  or or_5 (or_5_out[0], controlled_buffer_11_out[0], controlled_buffer_5_out[0]);
  not not_7 (not_7_out[0], controlled_buffer_12_out[0]);
  assign controlled_buffer_18_out = or_6_out ? clk : 1'bz;  // Controlled_Buffer controlled_buffer_18
  assign controlled_buffer_15_out = psh ? out_14 : 8'bz;  // Controlled_Buffer controlled_buffer_19
  or or_6 (or_6_out, ld, psh);
  LED led_1 (.in(n8bit_adder_1_out_18));
  assign controlled_buffer_20_out = or_3_out ? n8bit_adder_1_out_26 : 8'bz;  // Controlled_Buffer controlled_buffer_20
  assign controlled_buffer_20_out = cmp ? {n8bit_comperator_1_out_17, {5{1'b0}}} : 8'bz;  // Controlled_Buffer controlled_buffer_21
  assign controlled_buffer_20_out = \and  ? and_6_out : 8'bz;  // Controlled_Buffer controlled_buffer_22
  assign controlled_buffer_20_out = \or  ? or_5_out : 8'bz;  // Controlled_Buffer controlled_buffer_23
  assign controlled_buffer_20_out = \not  ? not_7_out : 8'bz;  // Controlled_Buffer controlled_buffer_24
  RAM #(.dataWidth(14)) ram_2 (
    .addr(controlled_buffer_6_out), .data(out_10), .clk(update), .ld(not_4_out), .clr(clear));  // open: sel
  assign controlled_buffer_25_out = not_5_out ? clk : 1'bz;  // Controlled_Buffer controlled_buffer_25
  _8bit_register akku (
    .in_1(controlled_buffer_18_out), .in_2(controlled_buffer_15_out[7]), .in_3(controlled_buffer_15_out[6]),
    .in_4(controlled_buffer_15_out[5]), .in_5(controlled_buffer_15_out[4]),
    .in_6(controlled_buffer_15_out[3]), .in_7(controlled_buffer_15_out[2]),
    .in_8(controlled_buffer_15_out[1]), .in_9(controlled_buffer_15_out[0]), .out_10(out_11[7]),
    .out_11(out_11[6]), .out_12(out_11[5]), .out_13(out_11[4]), .out_14(out_11[3]), .out_15(out_11[2]),
    .out_16(out_11[1]), .out_17(out_11[0]));
  assign out_13 = or_4_out ? controlled_buffer_15_out : 8'bz;  // Controlled_Buffer controlled_buffer_26
  _8bit_register result_reg (
    .in_1(clk), .in_2(controlled_buffer_20_out[7]), .in_3(controlled_buffer_20_out[6]),
    .in_4(controlled_buffer_20_out[5]), .in_5(controlled_buffer_20_out[4]),
    .in_6(controlled_buffer_20_out[3]), .in_7(controlled_buffer_20_out[2]),
    .in_8(controlled_buffer_20_out[1]), .in_9(controlled_buffer_20_out[0]), .out_10(out_14[7]),
    .out_11(out_14[6]), .out_12(out_14[5]), .out_13(out_14[4]), .out_14(out_14[3]), .out_15(out_14[2]),
    .out_16(out_14[1]), .out_17(out_14[0]));
  assign controlled_buffer_27_out = not_2_out ? out_10 : 14'bz;  // Controlled_Buffer controlled_buffer_27
  Register #(.width(14)) register_1 (
    .D(controlled_buffer_27_out),
    .Q({addr[0], addr[1], addr[2], addr[3], addr[4], addr[5], addr[6], addr[7], v_a, register_1_q}),
    .clk(controlled_buffer_25_out));  // open: en, clr
  not not_8 (not_8_out, register_1_q[0]);
  not not_9 (not_9_out, register_1_q[1]);
  not not_10 (not_10_out, register_1_q[2]);
  not not_11 (not_11_out, register_1_q[3]);
  not not_12 (not_12_out, register_1_q[4]);
  and and_7 (ld, not_12_out, not_11_out, not_10_out, not_9_out, not_8_out);
  and and_8 (st, register_1_q[4], not_11_out, not_10_out, not_9_out, not_8_out);
  and and_9 (add, not_12_out, not_11_out, register_1_q[2], not_9_out, not_8_out);
  and and_10 (sub, register_1_q[4], not_11_out, register_1_q[2], not_9_out, not_8_out);
  and and_11 (cmp, not_12_out, register_1_q[3], register_1_q[2], not_9_out, not_8_out);
  and and_12 (psh, register_1_q[4], register_1_q[3], register_1_q[2], not_9_out, not_8_out);
  and and_13 (\and , not_12_out, not_11_out, not_10_out, register_1_q[1], not_8_out);
  and and_14 (\or , register_1_q[4], not_11_out, not_10_out, register_1_q[1], not_8_out);
  and and_15 (\not , not_12_out, register_1_q[3], not_10_out, register_1_q[1], not_8_out);
  and and_16 (jlt, register_1_q[4], register_1_q[3], not_10_out, register_1_q[1], not_8_out);
  and and_17 (jgt, not_12_out, not_11_out, register_1_q[2], register_1_q[1], not_8_out);
  and and_18 (jeq, register_1_q[4], not_11_out, register_1_q[2], register_1_q[1], not_8_out);
  and and_19 (jmp, not_12_out, register_1_q[3], register_1_q[2], register_1_q[1], not_8_out);
  and and_20 (\end , register_1_q[4], register_1_q[3], register_1_q[2], register_1_q[1], not_8_out);
  and and_21 (out, not_12_out, not_11_out, not_10_out, not_9_out, register_1_q[0]);

  assign out_12 = out_11;

  // Other names for the same wires on the sheet: akku[7:0] = out_11; operand[7:0] = out_13; result[7:0] = out_14;
  //   val[7:0] = addr
endmodule

module _4bit_register (
  input  in_1,
  input  in_2,
  input  in_3,
  input  in_4,
  input  in_5,
  output out_6,
  output out_7,
  output out_8,
  output out_9
);

  D_Flip_Flop d_ff_1 (.clk(in_1), .D(in_2), .Q(out_6));  // open: Qn, preset, en, reset
  D_Flip_Flop d_ff_2 (.clk(in_1), .D(in_3), .Q(out_7));  // open: Qn, preset, en, reset
  D_Flip_Flop d_ff_3 (.clk(in_1), .D(in_4), .Q(out_8));  // open: Qn, preset, en, reset
  D_Flip_Flop d_ff_4 (.clk(in_1), .D(in_5), .Q(out_9));  // open: Qn, preset, en, reset
endmodule

module _8bit_register (
  input  in_1,
  input  in_2,
  input  in_3,
  input  in_4,
  input  in_5,
  input  in_6,
  input  in_7,
  input  in_8,
  input  in_9,
  output out_10,
  output out_11,
  output out_12,
  output out_13,
  output out_14,
  output out_15,
  output out_16,
  output out_17
);

  D_Flip_Flop d_ff_1 (.clk(in_1), .D(in_2), .Q(out_10));  // open: Qn, preset, en, reset
  D_Flip_Flop d_ff_2 (.clk(in_1), .D(in_3), .Q(out_11));  // open: Qn, preset, en, reset
  D_Flip_Flop d_ff_3 (.clk(in_1), .D(in_4), .Q(out_12));  // open: Qn, preset, en, reset
  D_Flip_Flop d_ff_4 (.clk(in_1), .D(in_5), .Q(out_13));  // open: Qn, preset, en, reset
  D_Flip_Flop d_ff_5 (.clk(in_1), .D(in_6), .Q(out_14));  // open: Qn, preset, en, reset
  D_Flip_Flop d_ff_6 (.clk(in_1), .D(in_7), .Q(out_15));  // open: Qn, preset, en, reset
  D_Flip_Flop d_ff_7 (.clk(in_1), .D(in_8), .Q(out_16));  // open: Qn, preset, en, reset
  D_Flip_Flop d_ff_8 (.clk(in_1), .D(in_9), .Q(out_17));  // open: Qn, preset, en, reset
endmodule

module _8bit_adder_2 (
  input  in_1,
  input  in_2,
  input  in_3,
  input  in_4,
  input  in_5,
  input  in_6,
  input  in_7,
  input  in_8,
  input  in_9,
  input  in_10,
  input  in_11,
  input  in_12,
  input  in_13,
  input  in_14,
  input  in_15,
  input  in_16,
  input  subtract,
  output out_18,
  output out_19,
  output out_20,
  output out_21,
  output out_22,
  output out_23,
  output out_24,
  output out_25,
  output out_26
);

  wire and_1_out, and_2_out, and_3_out, and_4_out, and_5_out, and_6_out, and_7_out, and_8_out, and_9_out,
       and_10_out, and_11_out, and_12_out, and_13_out, and_14_out, and_15_out, and_16_out, or_2_out,
       or_3_out, or_4_out, or_5_out, or_6_out, or_7_out, or_8_out, xor_1_out, xor_2_out, xor_3_out,
       xor_4_out, xor_5_out, xor_6_out, xor_7_out, xor_8_out, xor_9_out, xor_10_out, xor_11_out, xor_12_out,
       xor_13_out, xor_14_out, xor_15_out, xor_16_out;

  xor xor_1 (xor_1_out, in_9, subtract);
  xor xor_2 (xor_2_out, in_10, subtract);
  xor xor_3 (xor_3_out, in_11, subtract);
  xor xor_4 (xor_4_out, in_12, subtract);
  xor xor_5 (xor_5_out, in_13, subtract);
  xor xor_6 (xor_6_out, in_14, subtract);
  xor xor_7 (xor_7_out, in_15, subtract);
  xor xor_8 (xor_8_out, in_16, subtract);
  and and_1 (and_1_out, or_3_out, in_2);
  and and_2 (and_2_out, or_4_out, xor_3_out);
  and and_3 (and_3_out, or_7_out, xor_6_out);
  and and_4 (and_4_out, or_8_out, xor_7_out);
  and and_5 (and_5_out, or_2_out, xor_1_out);
  xor xor_9 (xor_9_out, or_2_out, xor_1_out);
  xor xor_10 (xor_10_out, or_3_out, in_2);
  xor xor_11 (xor_11_out, or_4_out, xor_3_out);
  and and_6 (and_6_out, or_5_out, xor_4_out);
  xor xor_12 (xor_12_out, or_5_out, xor_4_out);
  and and_7 (and_7_out, or_6_out, xor_5_out);
  xor xor_13 (xor_13_out, or_6_out, xor_5_out);
  xor xor_14 (xor_14_out, or_7_out, xor_6_out);
  xor xor_15 (xor_15_out, or_8_out, xor_7_out);
  and and_8 (and_8_out, subtract, xor_8_out);
  xor xor_16 (xor_16_out, subtract, xor_8_out);
  and and_9 (and_9_out, xor_9_out, in_1);
  xor xor_17 (out_19, xor_9_out, in_1);
  and and_10 (and_10_out, xor_10_out, xor_2_out);
  xor xor_18 (out_20, xor_10_out, xor_2_out);
  and and_11 (and_11_out, xor_11_out, in_3);
  xor xor_19 (out_21, xor_11_out, in_3);
  and and_12 (and_12_out, xor_12_out, in_4);
  xor xor_20 (out_22, xor_12_out, in_4);
  and and_13 (and_13_out, xor_13_out, in_5);
  xor xor_21 (out_23, xor_13_out, in_5);
  and and_14 (and_14_out, xor_14_out, in_6);
  xor xor_22 (out_24, xor_14_out, in_6);
  and and_15 (and_15_out, xor_15_out, in_7);
  xor xor_23 (out_25, xor_15_out, in_7);
  and and_16 (and_16_out, xor_16_out, in_8);
  xor xor_24 (out_26, xor_16_out, in_8);
  or or_1 (out_18, and_9_out, and_5_out);
  or or_2 (or_2_out, and_10_out, and_1_out);
  or or_3 (or_3_out, and_11_out, and_2_out);
  or or_4 (or_4_out, and_12_out, and_6_out);
  or or_5 (or_5_out, and_13_out, and_7_out);
  or or_6 (or_6_out, and_14_out, and_3_out);
  or or_7 (or_7_out, and_15_out, and_4_out);
  or or_8 (or_8_out, and_16_out, and_8_out);
endmodule

module address_counter (
  input  clock,
  input  [7:0] val,
  input  subtract,
  input  [7:0] jump_to,
  input  jump_mode,
  output [7:0] out_6
);

  wire n8bit_adder_1_out_19, n8bit_adder_1_out_20, n8bit_adder_1_out_21, n8bit_adder_1_out_22,
       n8bit_adder_1_out_23, n8bit_adder_1_out_24, n8bit_adder_1_out_25, n8bit_adder_1_out_26, not_1_out;
  wire [7:0] controlled_buffer_1_out, multiplexer_1_out;

  Multiplexer #(.width(8)) multiplexer_1 (
    .in0(val), .in1({8{1'b0}}), .out(multiplexer_1_out), .sel(jump_mode));  // open: en
  _8bit_adder_2 u_8bit_adder_1 (
    .out_19(n8bit_adder_1_out_19), .out_20(n8bit_adder_1_out_20), .in_1(controlled_buffer_1_out[7]),
    .out_21(n8bit_adder_1_out_21), .in_2(controlled_buffer_1_out[6]), .in_3(controlled_buffer_1_out[5]),
    .in_4(controlled_buffer_1_out[4]), .out_22(n8bit_adder_1_out_22), .in_5(controlled_buffer_1_out[3]),
    .in_6(controlled_buffer_1_out[2]), .in_7(controlled_buffer_1_out[1]), .in_8(controlled_buffer_1_out[0]),
    .in_9(multiplexer_1_out[7]), .in_10(multiplexer_1_out[6]), .in_11(multiplexer_1_out[5]),
    .in_12(multiplexer_1_out[4]), .in_13(multiplexer_1_out[3]), .in_14(multiplexer_1_out[2]),
    .in_15(multiplexer_1_out[1]), .in_16(multiplexer_1_out[0]), .subtract(subtract),
    .out_23(n8bit_adder_1_out_23), .out_24(n8bit_adder_1_out_24), .out_25(n8bit_adder_1_out_25),
    .out_26(n8bit_adder_1_out_26));  // open: out_18
  assign controlled_buffer_1_out = jump_mode ? jump_to : 8'bz;  // Controlled_Buffer controlled_buffer_1
  _8bit_register u_8bit_register_1 (
    .in_1(clock), .in_2(n8bit_adder_1_out_19), .in_3(n8bit_adder_1_out_20), .in_4(n8bit_adder_1_out_21),
    .in_5(n8bit_adder_1_out_22), .in_6(n8bit_adder_1_out_23), .in_7(n8bit_adder_1_out_24),
    .in_8(n8bit_adder_1_out_25), .in_9(n8bit_adder_1_out_26), .out_10(out_6[7]), .out_11(out_6[6]),
    .out_12(out_6[5]), .out_13(out_6[4]), .out_14(out_6[3]), .out_15(out_6[2]), .out_16(out_6[1]),
    .out_17(out_6[0]));
  assign controlled_buffer_1_out = not_1_out ? out_6 : 8'bz;  // Controlled_Buffer controlled_buffer_2
  not not_1 (not_1_out, jump_mode);
endmodule

module _8bit_comperator (
  input  in_1,
  input  in_2,
  input  in_3,
  input  in_4,
  input  in_5,
  input  in_6,
  input  in_7,
  input  in_8,
  input  in_9,
  input  in_10,
  input  in_11,
  input  in_12,
  input  in_13,
  input  in_14,
  input  in_15,
  input  in_16,
  output out_17,
  output out_18,
  output out_19
);

  Comparator #(.mode("unsigned")) comparator_1 (
    .a({in_1, in_2, in_3, in_4, in_5, in_6, in_7, in_8}),
    .b({in_9, in_10, in_11, in_12, in_13, in_14, in_15, in_16}), .gt(out_17), .eq(out_18), .lt(out_19));
endmodule

module out_terminal (
  input  clear,
  input  clock,
  input  w_r,
  input  [7:0] data,
  input  scroll,
  input  scroll_direction_d_u,
  output [7:0] out_7,
  output [7:0] out_8
);

  wire controlled_buffer_2_out, not_1_out;
  wire [7:0] address_counter_out_6, controlled_buffer_1_out, controlled_buffer_3_out, controlled_buffer_4_out;

  assign controlled_buffer_1_out = not_1_out ? 8'h1 : 8'bz;  // Controlled_Buffer controlled_buffer_1
  assign controlled_buffer_2_out = not_1_out ? clock : 1'bz;  // Controlled_Buffer controlled_buffer_2
  not not_1 (not_1_out, w_r);
  address_counter address_counter (
    .clock(controlled_buffer_2_out), .val(controlled_buffer_1_out), .out_6(address_counter_out_6));  // open: subtract, jump_to, jump_mode
  address_counter address_counter_2 (
    .clock(scroll), .val(8'h1), .subtract(scroll_direction_d_u), .out_6(out_8), .jump_to({8{1'b0}}),
    .jump_mode(1'b0));
  assign controlled_buffer_3_out = not_1_out ? address_counter_out_6 : 8'bz;  // Controlled_Buffer controlled_buffer_3
  assign controlled_buffer_4_out = not_1_out ? data : 8'bz;  // Controlled_Buffer controlled_buffer_4
  assign controlled_buffer_3_out = w_r ? out_8 : 8'bz;  // Controlled_Buffer controlled_buffer_5
  RAM ram_1 (
    .addr(controlled_buffer_3_out), .data(controlled_buffer_4_out), .clk(controlled_buffer_2_out), .ld(w_r),
    .clr(clear));  // open: sel
  assign out_7 = w_r ? controlled_buffer_4_out : 8'bz;  // Controlled_Buffer controlled_buffer_6
endmodule
