// Logisim project von-neumann.circ as structural Verilog: 7 circuits, main circuit von-neumann
module von_neumann (
  input  writing_mode,
  input  [23:0] in_2,
  input  [14:0] in_3,
  input  clear,
  input  programming_mode,
  input  update,
  input  [14:0] in_7,
  input  in_8,
  input  in_9,
  output [23:0] out_10,
  output [14:0] out_11,
  output [14:0] out_12,
  output [14:0] out_13,
  output [23:0] out_14,
  output [14:0] out_15
);

  wire add, \and , and_1_out, and_2_out, and_3_out, and_4_out, and_5_out, button_1_out, clk, cmp,
       comparator_1_eq, comparator_2_eq, controlled_buffer_1_out, controlled_buffer_5_out,
       controlled_buffer_7_out, controlled_buffer_11_out, \end , jeq, jgt, jlt, jmp, ld,
       n15bit_adder_1_out_47, \not , not_1_out, not_2_out, not_3_out, not_4_out, not_5_out, not_6_out,
       not_7_out, not_8_out, not_9_out, not_10_out, not_11_out, \or , or_1_out, or_2_out, or_3_out, or_4_out,
       or_5_out, out, psh, st, sub, undriven;
  wire [2:0] n15bit_comperator_1_out_31;
  wire [14:0] and_21_out, controlled_buffer_2_out, controlled_buffer_8_out, controlled_buffer_14_out,
       controlled_buffer_15_out, controlled_buffer_16_out, controlled_buffer_18_out,
       controlled_buffer_19_out, controlled_buffer_20_out, controlled_buffer_21_out,
       controlled_buffer_22_out, controlled_buffer_23_out, n15bit_adder_1_out_32, not_12_out, op_counter,
       or_6_out, ram_1_data;
  wire [14:1] controlled_buffer_17_out;
  wire [23:0] controlled_buffer_10_out;

  Button button_1 (.out(button_1_out));
  not not_1 (not_1_out, button_1_out);
  and and_1 (and_1_out, jlt, out_11[2]);
  and and_2 (and_2_out, jgt, out_11[0]);
  and and_3 (and_3_out, jeq, out_11[1]);
  Clock #(.highDuration(10), .lowDuration(10)) clock_1 (.out(clk));
  Comparator #(.width(15), .mode("unsigned")) comparator_1 (
    .a(op_counter), .b({15{1'b0}}), .eq(comparator_1_eq));  // open: gt, lt
  and and_4 (and_4_out, comparator_1_eq, not_1_out);
  or or_1 (or_1_out, and_1_out, and_2_out, and_3_out, jmp, \end );
  Multiplexer multiplexer_1 (.in0(undriven), .in1(1'b0), .sel(and_4_out));  // open: out, en
  assign controlled_buffer_1_out = not_5_out ? clk : 1'bz;  // Controlled_Buffer controlled_buffer_1
  _15bit_address_counter operation_counter (
    .out_5(op_counter), .jump_mode(in_8), .rate(in_7),
    .jump_to({out_14[0], out_14[1], out_14[2], out_14[3], out_14[4], out_14[5], out_14[6], out_14[7], out_14[8], out_14[9], out_14[10], out_14[11], out_14[12], out_14[13], out_14[14]}),
    .clock(controlled_buffer_1_out));
  assign controlled_buffer_2_out = programming_mode ? in_3 : 15'bz;  // Controlled_Buffer controlled_buffer_2
  not not_2 (not_2_out, programming_mode);
  assign controlled_buffer_2_out = not_2_out ? op_counter : 15'bz;  // Controlled_Buffer controlled_buffer_3
  not not_3 (not_3_out, comparator_2_eq);
  Comparator #(.width(15), .mode("unsigned")) comparator_2 (
    .a(out_11), .b(out_13), .eq(comparator_2_eq));  // open: gt, lt
  assign out_10 = writing_mode ? in_2 : 24'bz;  // Controlled_Buffer controlled_buffer_4
  not not_4 (not_4_out, writing_mode);
  not not_5 (not_5_out, and_5_out);
  and and_5 (and_5_out, psh, not_3_out);
  or or_2 (or_2_out, ld, or_3_out);
  assign controlled_buffer_5_out = st ? clk : 1'bz;  // Controlled_Buffer controlled_buffer_5
  RAM #(.addrWidth(15), .dataWidth(15)) ram_1 (
    .addr({out_14[0], out_14[1], out_14[2], out_14[3], out_14[4], out_14[5], out_14[6], out_14[7], out_14[8], out_14[9], out_14[10], out_14[11], out_14[12], out_14[13], out_14[14]}),
    .data(ram_1_data), .clk(controlled_buffer_5_out), .ld(or_2_out));  // open: sel, clr
  assign ram_1_data = st ? out_11 : 15'bz;  // Controlled_Buffer controlled_buffer_6
  or or_3 (or_3_out, add, sub, cmp, \and , \or , \not );
  RAM #(.addrWidth(15), .dataWidth(24)) ram_2 (
    .addr(controlled_buffer_2_out), .data(out_10), .clk(update), .ld(not_4_out), .clr(clear));  // open: sel
  assign controlled_buffer_7_out = not_5_out ? clk : 1'bz;  // Controlled_Buffer controlled_buffer_7
  assign controlled_buffer_8_out = out_14[16] ? {out_14[0], out_14[1], out_14[2], out_14[3], out_14[4], out_14[5], out_14[6], out_14[7], out_14[8], out_14[9], out_14[10], out_14[11], out_14[12], out_14[13], out_14[14]} : 15'bz;  // Controlled_Buffer controlled_buffer_8
  not not_6 (not_6_out, out_14[16]);
  assign controlled_buffer_8_out = not_6_out ? ram_1_data : 15'bz;  // Controlled_Buffer controlled_buffer_9
  assign controlled_buffer_10_out = not_2_out ? out_10 : 24'bz;  // Controlled_Buffer controlled_buffer_10
  Register #(.width(24)) register_1 (
    .D(controlled_buffer_10_out), .Q(out_14), .clk(controlled_buffer_7_out));  // open: en, clr
  assign controlled_buffer_11_out = or_4_out ? clk : 1'bz;  // Controlled_Buffer controlled_buffer_11
  assign controlled_buffer_8_out = psh ? out_13 : 15'bz;  // Controlled_Buffer controlled_buffer_12
  or or_4 (or_4_out, ld, psh);
  _15bit_register u_15bit_register_1 (
    .in_1(controlled_buffer_11_out), .in_2(controlled_buffer_8_out[0]), .in_3(controlled_buffer_8_out[1]),
    .in_4(controlled_buffer_8_out[2]), .in_5(controlled_buffer_8_out[3]), .in_6(controlled_buffer_8_out[4]),
    .in_7(controlled_buffer_8_out[5]), .in_8(controlled_buffer_8_out[6]), .in_9(controlled_buffer_8_out[7]),
    .in_10(controlled_buffer_8_out[8]), .in_11(controlled_buffer_8_out[9]),
    .in_12(controlled_buffer_8_out[10]), .in_13(controlled_buffer_8_out[11]),
    .in_14(controlled_buffer_8_out[12]), .in_15(controlled_buffer_8_out[13]),
    .in_16(controlled_buffer_8_out[14]), .out_17(out_11[0]), .out_18(out_11[1]), .out_19(out_11[2]),
    .out_20(out_11[3]), .out_21(out_11[4]), .out_22(out_11[5]), .out_23(out_11[6]), .out_24(out_11[7]),
    .out_25(out_11[8]), .out_26(out_11[9]), .out_27(out_11[10]), .out_28(out_11[11]), .out_29(out_11[12]),
    .out_30(out_11[13]), .out_31(out_11[14]));
  assign out_12 = or_3_out ? controlled_buffer_8_out : 15'bz;  // Controlled_Buffer controlled_buffer_13
  not not_7 (not_7_out, out_14[21]);
  not not_8 (not_8_out, out_14[20]);
  not not_9 (not_9_out, out_14[19]);
  not not_10 (not_10_out, out_14[18]);
  not not_11 (not_11_out, out_14[17]);
  and and_6 (ld, not_11_out, not_10_out, not_9_out, not_8_out, not_7_out);
  and and_7 (st, out_14[17], not_10_out, not_9_out, not_8_out, not_7_out);
  and and_8 (add, not_11_out, not_10_out, out_14[19], not_8_out, not_7_out);
  and and_9 (sub, out_14[17], not_10_out, out_14[19], not_8_out, not_7_out);
  and and_10 (cmp, not_11_out, out_14[18], out_14[19], not_8_out, not_7_out);
  and and_11 (psh, out_14[17], out_14[18], out_14[19], not_8_out, not_7_out);
  and and_12 (\and , not_11_out, not_10_out, not_9_out, out_14[20], not_7_out);
  and and_13 (\or , out_14[17], not_10_out, not_9_out, out_14[20], not_7_out);
  and and_14 (\not , not_11_out, out_14[18], not_9_out, out_14[20], not_7_out);
  and and_15 (jlt, out_14[17], out_14[18], not_9_out, out_14[20], not_7_out);
  and and_16 (jgt, not_11_out, not_10_out, out_14[19], out_14[20], not_7_out);
  and and_17 (jeq, out_14[17], not_10_out, out_14[19], out_14[20], not_7_out);
  and and_18 (jmp, not_11_out, out_14[18], out_14[19], out_14[20], not_7_out);
  and and_19 (\end , out_14[17], out_14[18], out_14[19], out_14[20], not_7_out);
  and and_20 (out, not_11_out, not_10_out, not_9_out, not_8_out, out_14[21]);
  or or_5 (or_5_out, add, sub);
  assign controlled_buffer_14_out = or_5_out ? out_11 : 15'bz;  // Controlled_Buffer controlled_buffer_14
  assign controlled_buffer_15_out = or_5_out ? out_12 : 15'bz;  // Controlled_Buffer controlled_buffer_15
  assign controlled_buffer_16_out = \and  ? out_12 : 15'bz;  // Controlled_Buffer controlled_buffer_16
  assign {controlled_buffer_17_out, controlled_buffer_17_out[1]} = \or  ? out_12 : 15'bz;  // Controlled_Buffer controlled_buffer_17
  assign controlled_buffer_18_out = cmp ? out_11 : 15'bz;  // Controlled_Buffer controlled_buffer_18
  assign controlled_buffer_19_out = cmp ? out_12 : 15'bz;  // Controlled_Buffer controlled_buffer_19
  assign controlled_buffer_20_out = \and  ? out_11 : 15'bz;  // Controlled_Buffer controlled_buffer_20
  assign controlled_buffer_21_out = \or  ? out_11 : 15'bz;  // Controlled_Buffer controlled_buffer_21
  assign controlled_buffer_22_out = \not  ? out_12 : 15'bz;  // Controlled_Buffer controlled_buffer_22
  _15bit_adder u_15bit_adder_1 (
    .subtract(sub), .in_17(controlled_buffer_14_out[0]), .in_18(controlled_buffer_14_out[1]),
    .in_19(controlled_buffer_14_out[2]), .in_20(controlled_buffer_14_out[3]),
    .in_21(controlled_buffer_14_out[4]), .in_22(controlled_buffer_14_out[5]),
    .in_23(controlled_buffer_14_out[6]), .in_24(controlled_buffer_14_out[7]),
    .in_25(controlled_buffer_14_out[8]), .in_26(controlled_buffer_14_out[9]),
    .in_27(controlled_buffer_14_out[10]), .in_28(controlled_buffer_14_out[11]),
    .in_29(controlled_buffer_14_out[12]), .in_30(controlled_buffer_14_out[13]),
    .in_31(controlled_buffer_14_out[14]), .in_2(controlled_buffer_15_out[0]),
    .in_3(controlled_buffer_15_out[1]), .in_4(controlled_buffer_15_out[2]),
    .in_5(controlled_buffer_15_out[3]), .in_6(controlled_buffer_15_out[4]),
    .in_7(controlled_buffer_15_out[5]), .in_8(controlled_buffer_15_out[6]),
    .in_9(controlled_buffer_15_out[7]), .in_10(controlled_buffer_15_out[8]),
    .in_11(controlled_buffer_15_out[9]), .in_12(controlled_buffer_15_out[10]),
    .in_13(controlled_buffer_15_out[11]), .in_14(controlled_buffer_15_out[12]),
    .in_15(controlled_buffer_15_out[13]), .in_16(controlled_buffer_15_out[14]),
    .out_32(n15bit_adder_1_out_32[0]), .out_33(n15bit_adder_1_out_32[1]), .out_34(n15bit_adder_1_out_32[2]),
    .out_35(n15bit_adder_1_out_32[3]), .out_36(n15bit_adder_1_out_32[4]), .out_37(n15bit_adder_1_out_32[5]),
    .out_38(n15bit_adder_1_out_32[6]), .out_39(n15bit_adder_1_out_32[7]), .out_40(n15bit_adder_1_out_32[8]),
    .out_41(n15bit_adder_1_out_32[9]), .out_42(n15bit_adder_1_out_32[10]),
    .out_43(n15bit_adder_1_out_32[11]), .out_44(n15bit_adder_1_out_32[12]),
    .out_45(n15bit_adder_1_out_32[13]), .out_46(n15bit_adder_1_out_32[14]), .out_47(n15bit_adder_1_out_47));
  LED led_1 (.in(n15bit_adder_1_out_47));
  _15bit_comperator u_15bit_comperator_1 (
    .in_1(controlled_buffer_18_out[0]), .in_2(controlled_buffer_18_out[1]),
    .in_3(controlled_buffer_18_out[2]), .in_4(controlled_buffer_18_out[3]),
    .in_5(controlled_buffer_18_out[4]), .in_6(controlled_buffer_18_out[5]),
    .in_7(controlled_buffer_18_out[6]), .in_8(controlled_buffer_18_out[7]),
    .in_9(controlled_buffer_18_out[8]), .in_10(controlled_buffer_18_out[9]),
    .in_11(controlled_buffer_18_out[10]), .in_12(controlled_buffer_18_out[11]),
    .in_13(controlled_buffer_18_out[12]), .in_14(controlled_buffer_18_out[13]),
    .in_15(controlled_buffer_18_out[14]), .in_16(controlled_buffer_19_out[0]),
    .in_17(controlled_buffer_19_out[1]), .in_18(controlled_buffer_19_out[2]),
    .in_19(controlled_buffer_19_out[3]), .in_20(controlled_buffer_19_out[4]),
    .in_21(controlled_buffer_19_out[5]), .in_22(controlled_buffer_19_out[6]),
    .in_23(controlled_buffer_19_out[7]), .in_24(controlled_buffer_19_out[8]),
    .in_25(controlled_buffer_19_out[9]), .in_26(controlled_buffer_19_out[10]),
    .in_27(controlled_buffer_19_out[11]), .in_28(controlled_buffer_19_out[12]),
    .in_29(controlled_buffer_19_out[13]), .in_30(controlled_buffer_19_out[14]),
    .out_31(n15bit_comperator_1_out_31[0]), .out_32(n15bit_comperator_1_out_31[1]),
    .out_33(n15bit_comperator_1_out_31[2]));
  assign controlled_buffer_23_out = or_5_out ? n15bit_adder_1_out_32 : 15'bz;  // Controlled_Buffer controlled_buffer_23
  assign controlled_buffer_23_out = cmp ? {{12{1'b0}}, n15bit_comperator_1_out_31} : 15'bz;  // Controlled_Buffer controlled_buffer_24
  and and_21 (and_21_out[0], controlled_buffer_20_out[0], controlled_buffer_16_out[0]);
  or or_6 (or_6_out[0], controlled_buffer_21_out[0], controlled_buffer_17_out[1]);
  not not_12 (not_12_out[0], controlled_buffer_22_out[0]);
  assign controlled_buffer_23_out = \and  ? and_21_out : 15'bz;  // Controlled_Buffer controlled_buffer_25
  assign controlled_buffer_23_out = \or  ? or_6_out : 15'bz;  // Controlled_Buffer controlled_buffer_26
  assign controlled_buffer_23_out = \not  ? not_12_out : 15'bz;  // Controlled_Buffer controlled_buffer_27
  _15bit_register result_reg (
    .in_1(clk), .in_2(controlled_buffer_23_out[0]), .in_3(controlled_buffer_23_out[1]),
    .in_4(controlled_buffer_23_out[2]), .in_5(controlled_buffer_23_out[3]),
    .in_6(controlled_buffer_23_out[4]), .in_7(controlled_buffer_23_out[5]),
    .in_8(controlled_buffer_23_out[6]), .in_9(controlled_buffer_23_out[7]),
    .in_10(controlled_buffer_23_out[8]), .in_11(controlled_buffer_23_out[9]),
    .in_12(controlled_buffer_23_out[10]), .in_13(controlled_buffer_23_out[11]),
    .in_14(controlled_buffer_23_out[12]), .in_15(controlled_buffer_23_out[13]),
    .in_16(controlled_buffer_23_out[14]), .out_17(out_13[0]), .out_18(out_13[1]), .out_19(out_13[2]),
    .out_20(out_13[3]), .out_21(out_13[4]), .out_22(out_13[5]), .out_23(out_13[6]), .out_24(out_13[7]),
    .out_25(out_13[8]), .out_26(out_13[9]), .out_27(out_13[10]), .out_28(out_13[11]), .out_29(out_13[12]),
    .out_30(out_13[13]), .out_31(out_13[14]));

  assign out_15 = out_11;

  // Other names for the same wires on the sheet: akku[14:0] = out_11; operand[14:0] = out_12; v_a = out_14[16];
  //   result[14:0] = out_13;
  //   addr[14:0] = {out_14[0], out_14[1], out_14[2], out_14[3], out_14[4], out_14[5], out_14[6], out_14[7], out_14[8], out_14[9], out_14[10], out_14[11], out_14[12], out_14[13], out_14[14]};
  //   val[14:0] = {out_14[0], out_14[1], out_14[2], out_14[3], out_14[4], out_14[5], out_14[6], out_14[7], out_14[8], out_14[9], out_14[10], out_14[11], out_14[12], out_14[13], out_14[14]}
endmodule

module _4bit_register (
  input  in_1,
  input  in_2,
  input  in_3,
  input  in_4,
  input  in_5,
  output out_6,
  output out_7,
  output out_8,
  output out_9
);

  D_Flip_Flop d_ff_1 (.clk(in_1), .D(in_2), .Q(out_6));  // open: Qn, preset, en, reset
  D_Flip_Flop d_ff_2 (.clk(in_1), .D(in_3), .Q(out_7));  // open: Qn, preset, en, reset
  D_Flip_Flop d_ff_3 (.clk(in_1), .D(in_4), .Q(out_8));  // open: Qn, preset, en, reset
  D_Flip_Flop d_ff_4 (.clk(in_1), .D(in_5), .Q(out_9));  // open: Qn, preset, en, reset
endmodule

module _15bit_register (
  input  in_1,
  input  in_2,
  input  in_3,
  input  in_4,
  input  in_5,
  input  in_6,
  input  in_7,
  input  in_8,
  input  in_9,
  input  in_10,
  input  in_11,
  input  in_12,
  input  in_13,
  input  in_14,
  input  in_15,
  input  in_16,
  output out_17,
  output out_18,
  output out_19,
  output out_20,
  output out_21,
  output out_22,
  output out_23,
  output out_24,
  output out_25,
  output out_26,
  output out_27,
  output out_28,
  output out_29,
  output out_30,
  output out_31
);

  D_Flip_Flop d_ff_1 (.clk(in_1), .D(in_2), .Q(out_17));  // open: Qn, preset, en, reset
  D_Flip_Flop d_ff_2 (.clk(in_1), .D(in_3), .Q(out_18));  // open: Qn, preset, en, reset
  D_Flip_Flop d_ff_3 (.clk(in_1), .D(in_4), .Q(out_19));  // open: Qn, preset, en, reset
  D_Flip_Flop d_ff_4 (.clk(in_1), .D(in_5), .Q(out_20));  // open: Qn, preset, en, reset
  D_Flip_Flop d_ff_5 (.clk(in_1), .D(in_6), .Q(out_21));  // open: Qn, preset, en, reset
  D_Flip_Flop d_ff_6 (.clk(in_1), .D(in_7), .Q(out_22));  // open: Qn, preset, en, reset
  D_Flip_Flop d_ff_7 (.clk(in_1), .D(in_8), .Q(out_23));  // open: Qn, preset, en, reset
  D_Flip_Flop d_ff_8 (.clk(in_1), .D(in_9), .Q(out_24));  // open: Qn, preset, en, reset
  D_Flip_Flop d_ff_9 (.clk(in_1), .D(in_10), .Q(out_25));  // open: Qn, preset, en, reset
  D_Flip_Flop d_ff_10 (.clk(in_1), .D(in_11), .Q(out_26));  // open: Qn, preset, en, reset
  D_Flip_Flop d_ff_11 (.clk(in_1), .D(in_12), .Q(out_27));  // open: Qn, preset, en, reset
  D_Flip_Flop d_ff_12 (.clk(in_1), .D(in_13), .Q(out_28));  // open: Qn, preset, en, reset
  D_Flip_Flop d_ff_13 (.clk(in_1), .D(in_14), .Q(out_29));  // open: Qn, preset, en, reset
  D_Flip_Flop d_ff_14 (.clk(in_1), .D(in_15), .Q(out_30));  // open: Qn, preset, en, reset
  D_Flip_Flop d_ff_15 (.clk(in_1), .D(in_16), .Q(out_31));  // open: Qn, preset, en, reset
endmodule

module _15bit_adder (
  input  subtract,
  input  in_2,
  input  in_3,
  input  in_4,
  input  in_5,
  input  in_6,
  input  in_7,
  input  in_8,
  input  in_9,
  input  in_10,
  input  in_11,
  input  in_12,
  input  in_13,
  input  in_14,
  input  in_15,
  input  in_16,
  input  in_17,
  input  in_18,
  input  in_19,
  input  in_20,
  input  in_21,
  input  in_22,
  input  in_23,
  input  in_24,
  input  in_25,
  input  in_26,
  input  in_27,
  input  in_28,
  input  in_29,
  input  in_30,
  input  in_31,
  output out_32,
  output out_33,
  output out_34,
  output out_35,
  output out_36,
  output out_37,
  output out_38,
  output out_39,
  output out_40,
  output out_41,
  output out_42,
  output out_43,
  output out_44,
  output out_45,
  output out_46,
  output out_47
);

  wire [14:0] xor_1_out;

  xor xor_1 (xor_1_out[0], in_17, subtract);
  xor xor_2 (xor_1_out[1], in_18, subtract);
  xor xor_3 (xor_1_out[2], in_19, subtract);
  xor xor_4 (xor_1_out[3], in_20, subtract);
  xor xor_5 (xor_1_out[4], in_21, subtract);
  xor xor_6 (xor_1_out[5], in_22, subtract);
  xor xor_7 (xor_1_out[6], in_23, subtract);
  xor xor_8 (xor_1_out[7], in_24, subtract);
  xor xor_9 (xor_1_out[8], in_25, subtract);
  xor xor_10 (xor_1_out[9], in_26, subtract);
  xor xor_11 (xor_1_out[10], in_27, subtract);
  xor xor_12 (xor_1_out[11], in_28, subtract);
  xor xor_13 (xor_1_out[12], in_29, subtract);
  xor xor_14 (xor_1_out[13], in_30, subtract);
  xor xor_15 (xor_1_out[14], in_31, subtract);
  Adder #(.width(15)) adder_1 (
    .a({in_16, in_15, in_14, in_13, in_12, in_11, in_10, in_9, in_8, in_7, in_6, in_5, in_4, in_3, in_2}),
    .b(xor_1_out),
    .out({out_46, out_45, out_44, out_43, out_42, out_41, out_40, out_39, out_38, out_37, out_36, out_35, out_34, out_33, out_32}),
    .cin(subtract), .cout(out_47));
endmodule

module _15bit_address_counter (
  input  clock,
  input  [14:0] rate,
  input  [14:0] jump_to,
  input  jump_mode,
  output [14:0] out_5
);

  wire n15bit_adder_1_out_32, n15bit_adder_1_out_33, n15bit_adder_1_out_34, n15bit_adder_1_out_35,
       n15bit_adder_1_out_36, n15bit_adder_1_out_37, n15bit_adder_1_out_38, n15bit_adder_1_out_39,
       n15bit_adder_1_out_40, n15bit_adder_1_out_41, n15bit_adder_1_out_42, n15bit_adder_1_out_43,
       n15bit_adder_1_out_44, n15bit_adder_1_out_45, n15bit_adder_1_out_46, not_1_out;
  wire [14:0] controlled_buffer_1_out, multiplexer_1_out;

  Multiplexer #(.width(15)) multiplexer_1 (
    .in0(rate), .in1({15{1'b0}}), .out(multiplexer_1_out), .sel(jump_mode));  // open: en
  _15bit_adder u_15bit_adder_1 (
    .subtract(1'b0), .in_17(controlled_buffer_1_out[0]), .in_18(controlled_buffer_1_out[1]),
    .in_19(controlled_buffer_1_out[2]), .in_20(controlled_buffer_1_out[3]),
    .in_21(controlled_buffer_1_out[4]), .in_22(controlled_buffer_1_out[5]),
    .in_23(controlled_buffer_1_out[6]), .in_24(controlled_buffer_1_out[7]),
    .in_25(controlled_buffer_1_out[8]), .in_26(controlled_buffer_1_out[9]),
    .in_27(controlled_buffer_1_out[10]), .in_28(controlled_buffer_1_out[11]),
    .in_29(controlled_buffer_1_out[12]), .in_30(controlled_buffer_1_out[13]),
    .in_31(controlled_buffer_1_out[14]), .in_2(multiplexer_1_out[0]), .in_3(multiplexer_1_out[1]),
    .in_4(multiplexer_1_out[2]), .in_5(multiplexer_1_out[3]), .in_6(multiplexer_1_out[4]),
    .in_7(multiplexer_1_out[5]), .in_8(multiplexer_1_out[6]), .in_9(multiplexer_1_out[7]),
    .in_10(multiplexer_1_out[8]), .in_11(multiplexer_1_out[9]), .in_12(multiplexer_1_out[10]),
    .in_13(multiplexer_1_out[11]), .in_14(multiplexer_1_out[12]), .in_15(multiplexer_1_out[13]),
    .in_16(multiplexer_1_out[14]), .out_32(n15bit_adder_1_out_32), .out_33(n15bit_adder_1_out_33),
    .out_34(n15bit_adder_1_out_34), .out_35(n15bit_adder_1_out_35), .out_36(n15bit_adder_1_out_36),
    .out_37(n15bit_adder_1_out_37), .out_38(n15bit_adder_1_out_38), .out_39(n15bit_adder_1_out_39),
    .out_40(n15bit_adder_1_out_40), .out_41(n15bit_adder_1_out_41), .out_42(n15bit_adder_1_out_42),
    .out_43(n15bit_adder_1_out_43), .out_44(n15bit_adder_1_out_44), .out_45(n15bit_adder_1_out_45),
    .out_46(n15bit_adder_1_out_46));  // open: out_47
  assign controlled_buffer_1_out = jump_mode ? jump_to : 15'bz;  // Controlled_Buffer controlled_buffer_1
  _15bit_register u_15bit_register_1 (
    .in_1(clock), .in_2(n15bit_adder_1_out_32), .in_3(n15bit_adder_1_out_33), .in_4(n15bit_adder_1_out_34),
    .in_5(n15bit_adder_1_out_35), .in_6(n15bit_adder_1_out_36), .in_7(n15bit_adder_1_out_37),
    .in_8(n15bit_adder_1_out_38), .in_9(n15bit_adder_1_out_39), .in_10(n15bit_adder_1_out_40),
    .in_11(n15bit_adder_1_out_41), .in_12(n15bit_adder_1_out_42), .in_13(n15bit_adder_1_out_43),
    .in_14(n15bit_adder_1_out_44), .in_15(n15bit_adder_1_out_45), .in_16(n15bit_adder_1_out_46),
    .out_17(out_5[0]), .out_18(out_5[1]), .out_19(out_5[2]), .out_20(out_5[3]), .out_21(out_5[4]),
    .out_22(out_5[5]), .out_23(out_5[6]), .out_24(out_5[7]), .out_25(out_5[8]), .out_26(out_5[9]),
    .out_27(out_5[10]), .out_28(out_5[11]), .out_29(out_5[12]), .out_30(out_5[13]), .out_31(out_5[14]));
  assign controlled_buffer_1_out = not_1_out ? out_5 : 15'bz;  // Controlled_Buffer controlled_buffer_2
  not not_1 (not_1_out, jump_mode);
endmodule

module _15bit_comperator (
  input  in_1,
  input  in_2,
  input  in_3,
  input  in_4,
  input  in_5,
  input  in_6,
  input  in_7,
  input  in_8,
  input  in_9,
  input  in_10,
  input  in_11,
  input  in_12,
  input  in_13,
  input  in_14,
  input  in_15,
  input  in_16,
  input  in_17,
  input  in_18,
  input  in_19,
  input  in_20,
  input  in_21,
  input  in_22,
  input  in_23,
  input  in_24,
  input  in_25,
  input  in_26,
  input  in_27,
  input  in_28,
  input  in_29,
  input  in_30,
  output out_31,
  output out_32,
  output out_33
);

  Comparator #(.width(15), .mode("unsigned")) comparator_1 (
    .a({in_15, in_14, in_13, in_12, in_11, in_10, in_9, in_8, in_7, in_6, in_5, in_4, in_3, in_2, in_1}),
    .b({in_30, in_29, in_28, in_27, in_26, in_25, in_24, in_23, in_22, in_21, in_20, in_19, in_18, in_17, in_16}),
    .gt(out_31), .eq(out_32), .lt(out_33));
endmodule

module out_terminal (
  input  clear,
  input  clock,
  input  w_r,
  input  [7:0] data,
  input  scroll,
  input  scroll_direction_d_u,
  output [7:0] out_7,
  output [7:0] out_8
);

  wire controlled_buffer_2_out, not_1_out;
  wire [7:0] address_counter_p3, controlled_buffer_1_out, controlled_buffer_3_out, controlled_buffer_4_out;

  assign controlled_buffer_1_out = not_1_out ? 8'h1 : 8'bz;  // Controlled_Buffer controlled_buffer_1
  assign controlled_buffer_2_out = not_1_out ? clock : 1'bz;  // Controlled_Buffer controlled_buffer_2
  not not_1 (not_1_out, w_r);
  // _15bit_address_counter address_counter: pin names not known; wires that end beside it: controlled_buffer_2_out, controlled_buffer_1_out, address_counter_p3
  // _15bit_address_counter address_counter_2: pin names not known; wires that end beside it: scroll, 8'h1, scroll_direction_d_u, {8{1'b0}}, 1'b0, out_8
  assign controlled_buffer_3_out = not_1_out ? address_counter_p3 : 8'bz;  // Controlled_Buffer controlled_buffer_3
  assign controlled_buffer_4_out = not_1_out ? data : 8'bz;  // Controlled_Buffer controlled_buffer_4
  assign controlled_buffer_3_out = w_r ? out_8 : 8'bz;  // Controlled_Buffer controlled_buffer_5
  RAM ram_1 (
    .addr(controlled_buffer_3_out), .data(controlled_buffer_4_out), .clk(controlled_buffer_2_out), .ld(w_r),
    .clr(clear));  // open: sel
  assign out_7 = w_r ? controlled_buffer_4_out : 8'bz;  // Controlled_Buffer controlled_buffer_6
endmodule
